// Digital circuit top.dig as structural Verilog
module top (
  input  clk
);

  wire C, pll_1_locked, R;

  PLL pll_1 (.clock_in(clk), .clock_out(C), .locked(pll_1_locked));
  not not_1 (R, pll_1_locked);
endmodule
